# Fritzing sketch cockpit-display-i2c (saved by Fritzing 0.9.3b)
circuit board: 8.46667cm x 5.64444cm
breadboards: 1

parts:
  Part1 = OLED Monochrome 128x64 1.3 inch [part_number=938]
  Part2 = Adafruit BMP180
  S1 = Pushbutton [package="[THT]"]
  S2 = Pushbutton [package="[THT]"]
  S3 = Pushbutton [package="[THT]"]
  JP1 = Header 1 [package=1x01_offset]
  JP2 = Header 1 [package=1x01_offset]
  JP3 = Header 1 [package=1x01_offset]
  JP4 = Header 1 [package=1x01_offset]
  U1 = attiny85 [package=dip]

nets:
  N1: Part1.MOSI_SDA, Part1.SCLK_SCK, Part2.SCL, Part2.SDA, JP1.1, JP2.1, U1.Pin_5, U1.Pin_7
  VIN: Part1.VIN, Part2.+5V, JP3.1, U1.Pin_6, U1.Pin_8
  GND: Part1.GND, Part2.GND, JP4.1, U1.Pin_2, U1.Pin_4
  N2: S1.Pin_1, S1.Pin_2
  N3: S1.Pin_3, S1.Pin_4, S2.Pin_3, S2.Pin_4, S3.Pin_3, S3.Pin_4
  N4: S2.Pin_1, S2.Pin_2
  N5: S3.Pin_1, S3.Pin_2
  N6: U1.Pin_1, U1.Pin_3

custom parts:
  OLED Monochrome 128x64 1.3 inch: These displays are small, only about 1.3" diagonal, but very readable due to the high contrast of an OLED display. This display is made of 128x64 individual white OLED pixels, each one is turned on or off by the controller chip. Because the display makes its own light, no backlight is required. This reduces the power required to run the OLED and is why the display has such high contrast; we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
  Adafruit BMP180: This precision sensor from Bosch is the best low-cost sensing solution for measuring barometric pressure and temperature. Because pressure changes with altitude you can also use it as an altimeter! The sensor is soldered onto a PCB with a 3.3V regulator, I2C level shifter and pull-up resistors on the I2C pins. The BMP180 is the next-generation of sensors from Bosch, and replaces the BMP085.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
